// Logisim project Parte 3 - Projeto - Linsmar.circ as structural Verilog: 8 circuits, main circuit Junção ULA com Reg
module ULA (
  input  [7:0] Entrada_ULA_1,
  input  [7:0] Entrada_ULA_2,
  input  [3:0] Seletor_ULA,
  output [7:0] Saida_da_ULA
);

  wire comparator_1_eq, comparator_2_lt, comparator_3_eq, comparator_3_lt, NOR_out_2, or_2_out;
  wire [7:0] adder_1_out, and_1_out, bit_extender_1_out, bit_extender_2_out, bit_extender_3_out,
       bit_extender_4_out, divider_1_out, multiplier_1_out, or_1_out, subtractor_1_out;

  assign and_1_out = Entrada_ULA_1 & Entrada_ULA_2;  // AND_Gate and_1, 8 bits wide
  assign or_1_out = Entrada_ULA_2 | Entrada_ULA_1;  // OR_Gate or_1, 8 bits wide
  Porta_NOR_da_ULA NOR (.in_1(Entrada_ULA_1), .out_2(NOR_out_2));
  Adder adder_1 (.a(Entrada_ULA_1), .b(Entrada_ULA_2), .out(adder_1_out));  // open: cin, cout
  Subtractor subtractor_1 (.a(Entrada_ULA_1), .b(Entrada_ULA_2), .out(subtractor_1_out));  // open: bin, bout
  Multiplier multiplier_1 (.a(Entrada_ULA_1), .b(Entrada_ULA_2), .out(multiplier_1_out));  // open: cin, cout
  Divider divider_1 (.a(Entrada_ULA_1), .b(Entrada_ULA_2), .out(divider_1_out));  // open: upper, rem
  Comparator #(.mode("unsigned")) comparator_1 (
    .a(Entrada_ULA_1), .b(Entrada_ULA_2), .eq(comparator_1_eq));  // open: gt, lt
  Comparator #(.mode("unsigned")) comparator_2 (
    .a(Entrada_ULA_1), .b(Entrada_ULA_2), .lt(comparator_2_lt));  // open: gt, eq
  Comparator #(.mode("unsigned")) comparator_3 (
    .a(Entrada_ULA_1), .b(Entrada_ULA_2), .eq(comparator_3_eq), .lt(comparator_3_lt));  // open: gt
  assign bit_extender_1_out = {{7{1'b0}}, NOR_out_2};  // Bit_Extender bit_extender_1
  assign bit_extender_2_out = {{7{1'b0}}, comparator_1_eq};  // Bit_Extender bit_extender_2
  assign bit_extender_3_out = {{7{1'b0}}, comparator_2_lt};  // Bit_Extender bit_extender_3
  assign bit_extender_4_out = {{7{1'b0}}, or_2_out};  // Bit_Extender bit_extender_4
  or or_2 (or_2_out, comparator_3_eq, comparator_3_lt);
  Multiplexer #(.select(4), .width(8), .enable("false")) multiplexer_1 (
    .in0(and_1_out), .in1(or_1_out), .in2(bit_extender_1_out), .in3(adder_1_out), .in4(subtractor_1_out),
    .in5(multiplier_1_out), .in6(divider_1_out), .in7(bit_extender_2_out), .in8(bit_extender_3_out),
    .in9(bit_extender_4_out), .out(Saida_da_ULA), .sel(Seletor_ULA));  // open: in10, in11, in12, in13, in14, in15

  // Notes on the sheet:
  //   Código
  //   Operação
  //   00
  //   E bit-a-bit
  //   01
  //   OU bit-a-bit
  //   02
  //   Não lógico
  //   03
  //   Adição
  //   04
  //   Subtração
  //   05
  //   06
  //   Divisão
  //   07
  //   Igual
  //   Menor
  //   08
  //   09
  //   Multiplicação
  //   Menor ou igual
endmodule

module Porta_NOR_da_ULA (
  input  [7:0] in_1,
  output out_2
);

  and and_1 (out_2, ~in_1[0], ~in_1[1], ~in_1[2], ~in_1[3], ~in_1[4], ~in_1[5], ~in_1[6], ~in_1[7]);  // AND_Gate
endmodule

module Registradores (
  input  [7:0] RIN,
  input  RWctl,
  input  [3:0] RD,
  input  [3:0] RS1,
  input  [3:0] RS2,
  output Pino_R0,
  output [7:0] RX,
  output [7:0] RY
);

  wire clock_1_out, demultiplexer_1_out0, demultiplexer_1_out1, demultiplexer_1_out2, demultiplexer_1_out3,
       demultiplexer_1_out4, demultiplexer_1_out5, demultiplexer_1_out6, demultiplexer_1_out7,
       demultiplexer_1_out8, demultiplexer_1_out9, demultiplexer_1_out10, demultiplexer_1_out11,
       demultiplexer_1_out12, demultiplexer_1_out13, demultiplexer_1_out14, demultiplexer_1_out15, not_1_out;
  wire [7:0] R0, R1, R2, R3, R4, R5, R6, R7, R8, R9, R10, R11, R12, R13, R14, R15;

  _0_ou_1_R0 u_0_ou_1_r0_1 (.Entrada_0_OU_1(R0), .\Saída_0_OU_1 (Pino_R0));
  Clock clock_1 (.out(clock_1_out));
  Demultiplexer #(.select(4)) demultiplexer_1 (
    .out0(demultiplexer_1_out0), .out1(demultiplexer_1_out1), .out2(demultiplexer_1_out2),
    .out3(demultiplexer_1_out3), .out4(demultiplexer_1_out4), .out5(demultiplexer_1_out5),
    .out6(demultiplexer_1_out6), .out7(demultiplexer_1_out7), .out8(demultiplexer_1_out8),
    .out9(demultiplexer_1_out9), .out10(demultiplexer_1_out10), .out11(demultiplexer_1_out11),
    .out12(demultiplexer_1_out12), .out13(demultiplexer_1_out13), .out14(demultiplexer_1_out14),
    .out15(demultiplexer_1_out15), .in(not_1_out), .sel(RD));  // open: en
  not not_1 (not_1_out, RWctl);
  Register register_1 (.D(RIN), .en(demultiplexer_1_out0), .Q(R0), .clk(clock_1_out));  // open: clr
  Register register_2 (.D(RIN), .en(demultiplexer_1_out1), .Q(R1), .clk(clock_1_out));  // open: clr
  Register register_3 (.D(RIN), .en(demultiplexer_1_out2), .Q(R2), .clk(clock_1_out));  // open: clr
  Register register_4 (.D(RIN), .en(demultiplexer_1_out4), .Q(R4), .clk(clock_1_out));  // open: clr
  Register register_5 (.D(RIN), .en(demultiplexer_1_out3), .Q(R3), .clk(clock_1_out));  // open: clr
  Register register_6 (.D(RIN), .en(demultiplexer_1_out5), .Q(R5), .clk(clock_1_out));  // open: clr
  Register register_7 (.D(RIN), .en(demultiplexer_1_out6), .Q(R6), .clk(clock_1_out));  // open: clr
  Multiplexer #(.select(4), .width(8)) multiplexer_1 (
    .in0(R0), .in1(R1), .in2(R2), .in3(R3), .in4(R4), .in5(R5), .in6(R6), .in7(R7), .in8(R8), .in9(R9),
    .in10(R10), .in11(R11), .in12(R12), .in13(R13), .in14(R14), .in15(R15), .out(RX), .sel(RS1));  // open: en
  Multiplexer #(.select(4), .width(8)) multiplexer_2 (
    .in0(R0), .in1(R1), .in2(R2), .in3(R3), .in4(R4), .in5(R5), .in6(R6), .in7(R7), .in8(R8), .in9(R9),
    .in10(R10), .in11(R11), .in12(R12), .in13(R13), .in14(R14), .in15(R15), .out(RY), .sel(RS2));  // open: en
  Register register_8 (.D(RIN), .en(demultiplexer_1_out7), .Q(R7), .clk(clock_1_out));  // open: clr
  Register register_9 (.D(RIN), .en(demultiplexer_1_out9), .Q(R9), .clk(clock_1_out));  // open: clr
  Register register_10 (.D(RIN), .en(demultiplexer_1_out8), .Q(R8), .clk(clock_1_out));  // open: clr
  Register register_11 (.D(RIN), .en(demultiplexer_1_out10), .Q(R10), .clk(clock_1_out));  // open: clr
  Register register_12 (.D(RIN), .en(demultiplexer_1_out11), .Q(R11), .clk(clock_1_out));  // open: clr
  Register register_13 (.D(RIN), .en(demultiplexer_1_out13), .Q(R13), .clk(clock_1_out));  // open: clr
  Register register_14 (.D(RIN), .en(demultiplexer_1_out12), .Q(R12), .clk(clock_1_out));  // open: clr
  Register register_15 (.D(RIN), .en(demultiplexer_1_out14), .Q(R14), .clk(clock_1_out));  // open: clr
  Register register_16 (.D(RIN), .en(demultiplexer_1_out15), .Q(R15), .clk(clock_1_out));  // open: clr
endmodule

module _0_ou_1_R0 (
  input  [7:0] Entrada_0_OU_1,
  output \Saída_0_OU_1 
);

  or or_1 (\Saída_0_OU_1 , Entrada_0_OU_1[0], Entrada_0_OU_1[1], Entrada_0_OU_1[2], Entrada_0_OU_1[3], Entrada_0_OU_1[4], Entrada_0_OU_1[5], Entrada_0_OU_1[6], Entrada_0_OU_1[7]);
endmodule

module \Junção_ULA_com_Reg  (
  input  [3:0] RS1,
  input  [3:0] RS2,
  input  [3:0] RD,
  input  RWctl,
  input  [7:0] in_5,
  input  [3:0] \Seletor_Operação_ULA ,
  input  [3:0] in_7,
  output [7:0] RX,
  output R0,
  output [7:0] RY
);

  wire [7:0] multiplexer_1_out, Saida_ULA;

  Multiplexer #(.select(4), .width(8)) multiplexer_1 (
    .in0(Saida_ULA), .in1(in_5), .out(multiplexer_1_out), .sel(in_7));  // open: in2, in3, in4, in5, in6, in7, in8, in9, in10, in11, in12, in13, in14, in15, en
  Registradores REGS (
    .Pino_R0(R0), .RIN(multiplexer_1_out), .RWctl(RWctl), .RX(RX), .RY(RY), .RD(RD), .RS1(RS1), .RS2(RS2));
  ULA ULA (.Saida_da_ULA(Saida_ULA), .Entrada_ULA_1(RX), .Entrada_ULA_2(RY), .Seletor_ULA(\Seletor_Operação_ULA ));
endmodule

module CTLU (
  input  [3:0] in_1,
  input  R0,
  output RWctl,
  output [2:0] RINctl,
  output [1:0] out_5,
  output [1:0] RDctl,
  output RMctl_and_WMctl
);

  Comparator #(.width(4)) comparator_1 (.a(in_1), .b(4'b1100), .eq(RWctl));  // open: gt, lt
  Multiplexer #(.select(4), .width(3)) multiplexer_1 (
    .in0(3'b000), .in1(3'b000), .in2(3'b000), .in3(3'b000), .in4(3'b000), .in5(3'b000), .in6(3'b000),
    .in7(3'b000), .in8(3'b000), .in9(3'b000), .in10(3'b001), .in11(3'b010), .in12(3'b000), .in13(3'b011),
    .in14(3'b100), .in15(3'b111), .out(RINctl), .sel(in_1));  // open: en
  Multiplexer #(.select(4), .width(2)) multiplexer_2 (
    .in0(2'b00), .in1(2'b00), .in2(2'b00), .in3(2'b00), .in4(2'b00), .in5(2'b00), .in6(2'b00), .in7(2'b00),
    .in8(2'b00), .in9(2'b00), .in10(2'b00), .in11(2'b00), .in12(2'b10), .in13(2'b10), .in14(2'b01),
    .in15(2'b01), .out(RDctl), .sel(in_1));  // open: en
  Multiplexer #(.select(4)) multiplexer_3 (
    .in0(1'b0), .in1(1'b0), .in2(1'b0), .in3(1'b0), .in4(1'b0), .in5(1'b0), .in6(1'b0), .in7(1'b0),
    .in8(1'b0), .in9(1'b0), .in10(1'b1), .in11(1'b0), .in12(1'b1), .in13(1'b0), .in14(1'b0), .in15(1'b0),
    .out(RMctl_and_WMctl), .sel(in_1));  // open: en
  PCctl pcctl_1 (.Ope(in_1), .R0(R0), .PCctl(out_5));

  // Other names for the same wires on the sheet: Op[3:0] = in_1
endmodule

module PCctl (
  input  [3:0] Ope,
  input  R0,
  output [1:0] PCctl
);

  and and_1 (PCctl[1], ~Ope[0], Ope[1], Ope[2], Ope[3], R0);  // AND_Gate
  and and_2 (PCctl[0], ~Ope[0], Ope[1], Ope[2], Ope[3], ~R0);  // AND_Gate
endmodule

module Testes (
);

  ROM #(.dataWidth(12)) rom_1 ();  // open: addr, data, sel
  RAM ram_1 ();  // open: addr, data, sel, clk, ld, clr
endmodule
